# Fritzing sketch battery_management (saved by Fritzing 0.9.6b)
stripboards: 1

parts:
  Fuse1 = Fuse with Handler [part_number=Htc-15m]  # not connected
  S1 = Toggle Switch [package=THT]
  S2 = Toggle Switch [package=THT]
  BAT1 = 18650 battery holder [package=battery-18650-kit]
  BAT2 = 18650 battery holder [package=battery-18650-kit]

nets:
  N1: S1.L1, S2.L1
  N2: S1.COM, S2.COM
  N3: S1.L2, S2.L2
  N4: BAT1.-, BAT2.+

custom parts:
  18650 battery holder: 18650 Battery Holder
