# Fritzing sketch flyintelbot_core (saved by Fritzing 0.9.4)
breadboards: 1

parts:
  Raspberry_Pi_1 = Raspberry Pi 3 [part_number=RPI-3-V1.2]
  ADC1 = MCP3008 [package=dil16]
  Disp1 = LBT2088AH [part_number=LBT2088AH]
  U1 = MAX7219 [package=dil24]
  Part3 = Rotoshield - Motor driver shield for Arduino
  M1 = DC Motor
  M2 = DC Motor
  M3 = DC Motor
  M4 = DC Motor
  J5 = Infrared Proximity Sensor
  J6 = Infrared Proximity Sensor
  J7 = Infrared Proximity Sensor
  J8 = Infrared Proximity Sensor
  J9 = Infrared Proximity Sensor
  LED1 = LED - 5mm [color="Yellow (585nm)" package="5 mm [THT]"]
  LED2 = LED - 5mm [color="Blue (470nm)" package="5 mm [THT]"]
  R1 = Resistor [tolerance=±5% resistance=150 package=THT]
  R2 = Resistor [tolerance=±5% resistance=150 package=THT]
  C1 = Ceramic Capacitor [capacitance=100nF voltage=10V package="100 mil [THT, multilayer]"]

nets:
  N1: Raspberry_Pi_1.GPIO3, Raspberry_Pi_1.GPIO4, Part3.3
  N2: Raspberry_Pi_1.GPIO27, Raspberry_Pi_1.GPIO22, Part3.8
  N3: Raspberry_Pi_1.3V3, Raspberry_Pi_1.GPIO10, ADC1.Din, U1.DIN
  N4: Raspberry_Pi_1.GPIO9, ADC1.Dout
  N5: Raspberry_Pi_1.GPIO11, ADC1.CLK, U1.CLK
  N6: Raspberry_Pi_1.GND, Raspberry_Pi_1.ID_SD, Raspberry_Pi_1.GPIO16, Raspberry_Pi_1.GPIO25, Raspberry_Pi_1.GPIO23, Part3.1, Part3.5, Part3.7, R1.Pin_1
  N7: Raspberry_Pi_1.GPIO5, Part3.4
  N8: Raspberry_Pi_1.GPIO20, R2.Pin_1
  N9: Raspberry_Pi_1.ID_SC, Part3.2
  N10: Raspberry_Pi_1.GPIO7, U1.LOAD
  N11: Raspberry_Pi_1.GPIO8, ADC1.CS/SHDN
  N12: Raspberry_Pi_1.GPIO24, Part3.6
  N13: ADC1.CH0, J9.Vout
  N14: ADC1.CH1, J8.Vout
  N15: ADC1.CH2, J7.Vout
  N16: ADC1.CH3, J6.Vout
  N17: ADC1.CH4, J5.Vout
  GND: ADC1.DGND, ADC1.AGND, U1.GND2, J5.GND, J6.GND, J7.GND, J8.GND, J9.GND, LED1.cathode, LED2.cathode, C1.1
  VCC: ADC1.VREF, ADC1.VDD, J5.Vcc, J6.Vcc, C1.0
  N18: Disp1.pin_8, U1.SEGDP
  N19: Part3.M1-2, M3.pin_2
  N20: Part3.M1-1, M3.pin_1
  N21: Part3.M2-2, M4.pin_2
  N22: Part3.M2-1, M4.pin_1
  N23: Part3.M3-2, M1.pin_2
  N24: Part3.M3-1, M1.pin_1
  N25: Part3.M4-2, M2.pin_2
  N26: Part3.M4-1, M2.pin_1
  VCC_2: J7.Vcc, J8.Vcc, J9.Vcc
  N27: LED1.anode, R1.Pin_0
  N28: LED2.anode, R2.Pin_0

notes:
  Connected with off-the-shelf module, so details are omitted.
